# Fritzing sketch remote (saved by Fritzing 0.9.4)
breadboards: 1

parts:
  Bauteil1 = Arduino Nano (Rev3.0) (ICSP)
  Bauteil2 = Bluetooth HC-05 Macho
  S2 = Pushbutton [package="[SMD]"]
  R1 = Resistor [tolerance=±5% resistance=220 package="2512 [SMD]"]
  X1 = USB Connectors [package=usb-a-h]

nets:
  GND: Bauteil1.GND, Bauteil2.GND, R1.Pin_1, X1.GND
  N1: Bauteil1.D2, S2.Pin_3, S2.Pin_4, R1.Pin_0
  N2: Bauteil1.D10, Bauteil2.TXD
  N3: Bauteil1.D11/MOSI, Bauteil2.RXD
  5V: Bauteil1.5V, Bauteil2.VCC, S2.Pin_1, S2.Pin_2, X1.VBUS
